# Fritzing sketch Elpanna (saved by Fritzing 0.8.0b)
breadboards: 1

parts:
  R2 = Resistor [tolerance=±5% resistance=220 package=THT]
  J1 = shrouded pin header, 34 pins [form="♂ (shrouded male)"]
  LED1 = LED - 5mm [color="Red (633nm)" package="5 mm [THT]"]
  LED2 = LED - 5mm [color="Green (570nm)" package="5 mm [THT]"]
  IC1 = ULN2803A [package=THT]
  Arduino1 = Arduino
  R1 = Resistor [tolerance=±5% resistance=220 package=THT]
  R3 = Resistor [tolerance=±5% resistance=10k package=THT]

nets:
  N1: R2.Pin_0, LED1.cathode
  N2: R2.Pin_1, J1.pin17, IC1.0V, Arduino1.GND, R1.Pin_1, R3.Pin_0
  N3: J1.pin1, Arduino1.A0, R3.Pin_1
  N4: J1.pin3, IC1.Out_1
  N5: J1.pin4, IC1.Out_2
  N6: J1.pin5, IC1.Out_3
  N7: J1.pin6, IC1.Out_4
  N8: J1.pin7, IC1.Out_5
  N9: J1.pin8, IC1.Out_6
  N10: J1.pin9, IC1.Out_7
  N11: J1.pin10, IC1.Out_8
  N12: J1.pin16, IC1.COM_-_Common
  N13: J1.pin34, Arduino1.+5V
  N14: LED1.anode, Arduino1.D13
  N15: LED2.cathode, R1.Pin_0
  N16: LED2.anode, Arduino1.D12
  N17: IC1.In_1, Arduino1.D2
  N18: IC1.In_2, Arduino1.D3
  N19: IC1.In_3, Arduino1.D4
  N20: IC1.In_4, Arduino1.D5
  N21: IC1.In_5, Arduino1.D6
  N22: IC1.In_6, Arduino1.D7
  N23: IC1.In_7, Arduino1.D8
  N24: IC1.In_8, Arduino1.D9
